# Fritzing sketch base (saved by Fritzing 0.9.3b)
circuit board: 5.11902cm x 7.34134cm

parts:
  U8 = 2.5mm Audio Jack [package=stereojack2.5mm_smd]
  Part2 = Bluetooth HC-05 Macho
  J1 = Piezo Speaker
  Part3 = NRF24L01+ Breakout Board
  J2 = male pin header, 2 pins [form="♂ (male)"]
  J3 = male pin header, 2 pins [form="♂ (male)"]
  Part4 = Arduino Nano (Rev3.0)
  J4 = female pin header, 2 pins [form="♀ (female)"]
  R1 = Resistor [tolerance=±5% resistance=220 package=THT]
  R2 = Resistor [tolerance=±5% resistance=220 package=THT]
  R3 = Resistor [tolerance=±5% resistance=220 package=THT]
  Part5 = Arduino Nano (Rev3.0)  # not connected

nets:
  N1: U8.LEFT, U8.RIGHT, J1.pin2, R1.Pin_0
  GND: U8.SLEEVE, Part2.GND, J1.pin1, Part3.GND, Part4.GND, J4.pin1, R3.Pin_1
  N2: Part2.TXD, J2.pin2
  N3: Part2.RXD, R2.Pin_1, R3.Pin_0
  VCC: Part2.VCC, Part4.5V
  VCC_2: Part3.VCC, Part4.3V3
  N4: Part3.CE, Part4.D8
  N5: Part3.CS, Part4.D7
  N6: Part3.SCK, Part4.D13/SCK
  N7: Part3.MOSI, Part4.D11/MOSI
  N8: Part3.MISO, Part4.D12/MISO
  N9: J2.pin1, Part4.D0/RX
  N10: J3.pin1, Part4.D1/TX
  N11: J3.pin2, R2.Pin_0
  N12: Part4.D3, R1.Pin_1
  N13: Part4.VIN, J4.pin2

custom parts:
  Arduino Nano (Rev3.0): The Arduino Nano is a small, complete, and breadboard-friendly board based on the ATmega328 (Arduino Nano 3.0) or ATmega168 (Arduino Nano 2.x). It has more or less the same functionality of the Arduino Duemilanove, but in a different package. It lacks only a DC power jack, and works with a Mini-B USB cable instead of a standard one. The Nano was designed and is being produced by Gravitech.
