# Fritzing sketch client-03 (saved by Fritzing 0.9.3b)
circuit board: 3.87609cm x 2.53962cm

parts:
  R2 = Resistor [tolerance=±5% resistance=220 package=THT]
  J1 = female pin header, 2 pins [form="♀ (female)"]
  J2 = female pin header, 2 pins [form="♀ (female)"]
  J3 = female pin header, 2 pins [form="♀ (female)"]
  R3 = Resistor [tolerance=±5% resistance=220 package=THT]
  Part7 = Arduino Pro Mini v13
  Part3 = NRF24L01+ Breakout Board
  R4 = Resistor [tolerance=±5% resistance=22k package=THT]
  C1 = Electrolytic Capacitor [capacitance=10nF package="100 mil [THT, electrolytic]"]
  U1 = MIC [package=mic-9.7mm]

nets:
  GND: R2.Pin_0, J1.pin1, J2.pin1, J3.pin1, R3.Pin_0, Part7.GND, Part3.GND, U1.2
  N1: R2.Pin_1, J3.pin2, Part7.A0
  N2: J1.pin2, Part7.RAW
  N3: J2.pin2, R3.Pin_1, Part7.A1
  VCC: Part7.VCC, Part3.VCC, R4.Pin_0
  N4: Part7.D13/SCK, Part3.SCK
  N5: Part7.D12/MISO, Part3.MISO
  N6: Part7.D11_PWM/MOSI, Part3.MOSI
  N7: Part7.D8, Part3.CE
  N8: Part7.D7, Part3.CS
  N9: R4.Pin_1, C1.+, U1.1

custom parts:
  Arduino Pro Mini v13: It's blue! It's thin! It's the Arduino Pro Mini! SparkFun's minimal design approach to Arduino. This is a 5V Arduino running the 16MHz bootloader. Arduino Pro Mini does not come with connectors populated so that you can solder in any connector or wire with any orientation you need. We recommend first time Arduino users start with the Uno R3. It's a great board that will get you up and running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
