# Fritzing sketch client-04 (saved by Fritzing 0.9.3b)
circuit board: 2.78535cm x 1.78016cm

parts:
  Part7 = Arduino Pro Mini v13
  R4 = Resistor [tolerance=±5% resistance=22k package=THT]
  U1 = MIC [package=mic-9.7mm]
  C1 = Electrolytic Capacitor [capacitance=10nF package="100 mil [THT, electrolytic]"]
  Part8 = NRF24L01+ Breakout Board

nets:
  GND: Part7.GND, U1.2, Part8.GND
  VCC: Part7.VCC, R4.Pin_0, Part8.VCC
  N1: Part7.A0, C1.-
  N2: Part7.D13/SCK, Part8.SCK
  N3: Part7.D12/MISO, Part8.MISO
  N4: Part7.D11_PWM/MOSI, Part8.MOSI
  N5: Part7.D8, Part8.CE
  N6: Part7.D7, Part8.CS
  N7: R4.Pin_1, U1.1, C1.+

custom parts:
  Arduino Pro Mini v13: It's blue! It's thin! It's the Arduino Pro Mini! SparkFun's minimal design approach to Arduino. This is a 5V Arduino running the 16MHz bootloader. Arduino Pro Mini does not come with connectors populated so that you can solder in any connector or wire with any orientation you need. We recommend first time Arduino users start with the Uno R3. It's a great board that will get you up and running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
  NRF24L01+ Breakout Board: This breakout board is for the Nordic Semiconductor NRF24L01+ 2.4GHz RF transceiver IC.
