# Fritzing sketch min-nano (saved by Fritzing 0.9.3b)
circuit board: 5.84815cm x 4.95193cm

parts:
  LED1 = smd LED [color="Red (633nm)" package="0805 [SMD]"]
  Part3 = NRF24L01+ Breakout Board
  R1 = Resistor [tolerance=±5% resistance=220 package=THT]
  Part5 = Arduino Nano (Rev3.0)
  U1 = POT [package=3362u]
  R2 = Resistor [tolerance=±5% resistance=220 package=THT]
  J1 = female pin header, 2 pins [form="♀ (female)"]
  J2 = female pin header, 2 pins [form="♀ (female)"]

nets:
  GND: LED1.cathode, Part3.GND, Part5.GND, U1.A, R2.Pin_1, J1.pin2, J2.pin2
  N1: LED1.anode, R1.Pin_1
  VCC: Part3.VCC, Part5.3V3
  N2: Part3.CE, Part5.D8
  N3: Part3.CS, Part5.D7
  N4: Part3.SCK, Part5.D13/SCK
  N5: Part3.MOSI, Part5.D11/MOSI
  N6: Part3.MISO, Part5.D12/MISO
  N7: R1.Pin_0, Part5.D2
  N8: Part5.VIN, J1.pin1
  N9: Part5.A0, U1.S, R2.Pin_0
  N10: U1.E, J2.pin1
