# Fritzing sketch min-pro (saved by Fritzing 0.9.3b)
circuit board: 5.84815cm x 4.95193cm

parts:
  LED1 = smd LED [color="Red (633nm)" package="0805 [SMD]"]
  Part3 = NRF24L01+ Breakout Board
  R1 = Resistor [tolerance=±5% resistance=220 package=THT]
  U1 = POT [package=3362u]
  R2 = Resistor [tolerance=±5% resistance=220 package=THT]
  J1 = female pin header, 2 pins [form="♀ (female)"]
  J2 = female pin header, 2 pins [form="♀ (female)"]
  Part6 = Arduino Pro Mini v13
  U2 = POT [package=3362u]
  J3 = female pin header, 2 pins [form="♀ (female)"]
  R3 = Resistor [tolerance=±5% resistance=220 package=THT]

nets:
  N1: LED1.cathode, R1.Pin_1
  N2: LED1.anode, Part6.D10_PWM/SS
  GND: Part3.GND, R1.Pin_0, U1.A, R2.Pin_1, J1.pin2, J2.pin2, Part6.GND, U2.E, J3.pin2, R3.Pin_1
  VCC: Part3.VCC, Part6.VCC
  N3: Part3.CE, Part6.D8
  N4: Part3.CS, Part6.D7
  N5: Part3.SCK, Part6.D13/SCK
  N6: Part3.MOSI, Part6.D11_PWM/MOSI
  N7: Part3.MISO, Part6.D12/MISO
  N8: U1.E, J2.pin1
  N9: U1.S, R2.Pin_0, Part6.A0
  N10: J1.pin1, Part6.RAW
  N11: Part6.A1, U2.S, R3.Pin_0
  N12: U2.A, J3.pin1
