# Fritzing sketch pro-2 (saved by Fritzing 0.9.3b)
circuit board: 3.74195cm x 2.42082cm

parts:
  Part3 = NRF24L01+ Breakout Board
  R2 = Resistor [tolerance=±5% resistance=220 package=THT]
  J1 = female pin header, 2 pins [form="♀ (female)"]
  J2 = female pin header, 2 pins [form="♀ (female)"]
  J3 = female pin header, 2 pins [form="♀ (female)"]
  R3 = Resistor [tolerance=±5% resistance=220 package=THT]
  Part7 = Arduino Pro Mini v13

nets:
  GND: Part3.GND, R2.Pin_0, J1.pin1, J2.pin1, J3.pin1, R3.Pin_0, Part7.GND
  VCC: Part3.VCC, Part7.VCC
  N1: Part3.CE, Part7.D8
  N2: Part3.CS, Part7.D7
  N3: Part3.SCK, Part7.D13/SCK
  N4: Part3.MOSI, Part7.D11_PWM/MOSI
  N5: Part3.MISO, Part7.D12/MISO
  N6: R2.Pin_1, J3.pin2, Part7.A1
  N7: J1.pin2, Part7.RAW
  N8: J2.pin2, R3.Pin_1, Part7.A0

custom parts:
  Arduino Pro Mini v13: It's blue! It's thin! It's the Arduino Pro Mini! SparkFun's minimal design approach to Arduino. This is a 5V Arduino running the 16MHz bootloader. Arduino Pro Mini does not come with connectors populated so that you can solder in any connector or wire with any orientation you need. We recommend first time Arduino users start with the Uno R3. It's a great board that will get you up and running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
