# Fritzing sketch radar (saved by Fritzing 0.9.3b)
circuit board: 5.08176cm x 7.26657cm

parts:
  SW-1 = Vibration sensor module
  LED1 = smd LED [color="Red (633nm)" package="0805 [SMD]"]
  Part3 = NRF24L01+ Breakout Board
  Mic1 = KY-038
  Part4 = Arduino Pro Mini v13
  R1 = Resistor [tolerance=±5% resistance=220 package=THT]

nets:
  VCC: SW-1.vcc, Part3.VCC, Mic1.pin3, Part4.VCC
  GND: SW-1.Ground, LED1.cathode, Part3.GND, Mic1.pin2, Part4.GND
  N1: SW-1.Digital_output, Part4.D3_PWM
  N2: LED1.anode, R1.Pin_1
  N3: Part3.CE, Part4.D8
  N4: Part3.CS, Part4.D7
  N5: Part3.SCK, Part4.D13/SCK
  N6: Part3.MOSI, Part4.D11_PWM/MOSI
  N7: Part3.MISO, Part4.D12/MISO
  N8: Mic1.pin4, Part4.D4
  N9: Part4.D2, R1.Pin_0

custom parts:
  Vibration sensor module: Single-roller type full induction trigger switch. When no vibration or tilt, the product is ON conduction state, and in the steady state, when a vibration or tilt, the switch will be rendered instantly disconnect the conductive resistance increases, generating a current pulse signal, thereby triggering circuit. The default state of the swith is close Digital output Supply voltage:3.3V-5V On-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
  KY-038: ky-038 Microphone sound sensor module
