# Fritzing sketch server-02 (saved by Fritzing 0.9.3b)
circuit board: 7.46741cm x 8.2419cm

parts:
  J1 = Piezo Speaker
  Part3 = NRF24L01+ Breakout Board
  J4 = female pin header, 2 pins [form="♀ (female)"]
  R1 = Resistor [tolerance=±5% resistance=220 package=THT]
  S1 = Pushbutton [package="[THT]"]
  S2 = Pushbutton [package="[THT]"]
  S3 = Pushbutton [package="[THT]"]
  Squix1 = OLED 0.96" 128x64 I2C SSD1306
  S4 = Pushbutton [package="[THT]"]
  U8 = 2.5mm Audio Jack [package=stereojack2.5mm_smd]
  Part7 = Arduino Pro Mini v13
  U9 = AUDIO-JACK2 [package=audio-jack]  # not connected

nets:
  GND: J1.pin1, Part3.GND, J4.pin1, S1.Pin_3, S1.Pin_4, S2.Pin_1, S2.Pin_2, S3.Pin_3, S3.Pin_4, Squix1.GND, S4.Pin_1, S4.Pin_2, U8.SLEEVE, Part7.GND
  N1: J1.pin2, R1.Pin_0, U8.LEFT, U8.RIGHT
  VCC: Part3.VCC, Squix1.VCC, Part7.VCC
  N2: Part3.CE, Part7.D8
  N3: Part3.CS, Part7.D7
  N4: Part3.SCK, Part7.D13/SCK
  N5: Part3.MOSI, Part7.D11_PWM/MOSI
  N6: Part3.MISO, Part7.D12/MISO
  N7: J4.pin2, Part7.RAW
  N8: R1.Pin_1, Part7.D4
  N9: S1.Pin_1, S1.Pin_2, Part7.D2
  N10: S2.Pin_3, S2.Pin_4, Part7.D6_PWM
  N11: S3.Pin_1, S3.Pin_2, Part7.D3_PWM
  N12: Squix1.SCL, Part7.A5
  N13: Squix1.SCA, Part7.A4
  N14: S4.Pin_3, S4.Pin_4, Part7.D5_PWM

custom parts:
  Arduino Pro Mini v13: It's blue! It's thin! It's the Arduino Pro Mini! SparkFun's minimal design approach to Arduino. This is a 5V Arduino running the 16MHz bootloader. Arduino Pro Mini does not come with connectors populated so that you can solder in any connector or wire with any orientation you need. We recommend first time Arduino users start with the Uno R3. It's a great board that will get you up and running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
