# Fritzing sketch server-04 (saved by Fritzing 0.9.3b)
circuit board: 4.65588cm x 4.64267cm

parts:
  J4 = female pin header, 2 pins [form="♀ (female)"]
  Part7 = Arduino Pro Mini v13
  Part3 = NRF24L01+ Breakout Board
  Squix1 = OLED 0.96" 128x64 I2C SSD1306
  S1 = Pushbutton [package="[THT]"]
  S3 = Pushbutton [package="[THT]"]
  S2 = Pushbutton [package="[THT]"]
  S4 = Pushbutton [package="[THT]"]
  R1 = Resistor [tolerance=±5% resistance=220 package=THT]
  U9 = AUDIO-JACK2 [package=audio-jack]

nets:
  GND: J4.pin1, Part7.GND, Part3.GND, Squix1.GND, S1.Pin_3, S1.Pin_4, S3.Pin_3, S3.Pin_4, S2.Pin_1, S2.Pin_2, S4.Pin_1, S4.Pin_2, U9.SLEEVE
  N1: J4.pin2, Part7.RAW
  N2: Part7.A4, Squix1.SCA
  N3: Part7.A5, Squix1.SCL
  VCC: Part7.VCC, Part3.VCC, Squix1.VCC
  N4: Part7.D13/SCK, Part3.SCK
  N5: Part7.D12/MISO, Part3.MISO
  N6: Part7.D11_PWM/MOSI, Part3.MOSI
  N7: Part7.D8, Part3.CE
  N8: Part7.D7, Part3.CS
  N9: Part7.D6_PWM, S2.Pin_3, S2.Pin_4
  N10: Part7.D5_PWM, S4.Pin_3, S4.Pin_4
  N11: Part7.D4, R1.Pin_1
  N12: Part7.D3_PWM, S3.Pin_1, S3.Pin_2
  N13: Part7.D2, S1.Pin_1, S1.Pin_2
  N14: R1.Pin_0, U9.RING, U9.TIP

custom parts:
  Arduino Pro Mini v13: It's blue! It's thin! It's the Arduino Pro Mini! SparkFun's minimal design approach to Arduino. This is a 5V Arduino running the 16MHz bootloader. Arduino Pro Mini does not come with connectors populated so that you can solder in any connector or wire with any orientation you need. We recommend first time Arduino users start with the Uno R3. It's a great board that will get you up and running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
